# Fritzing sketch schematic (saved by Fritzing 1.0.6)
breadboards: 1

parts:
  BME280 = BME280 Breakout
  LED1 = RGB LED (com. cathode, rbg) [color="Red (633nm)" current=0.030A package="5 mm [THT]"]
  Part3 = Arduino Nano (Rev3.0)
  Display = Grove OLED 128x96
  soil_moisture_sensor = Soil Moisture Sensor
  R1 = Resistor [tolerance=±5% power=0.25W resistance=220 package=THT]
  R2 = Resistor [tolerance=±5% power=0.25W resistance=220 package=THT]
  R3 = Resistor [tolerance=±5% power=0.25W resistance=220 package=THT]
  servo = Dagu DGServo 9g (Top view) [part_number=RS001B]
  relai = KY-019 5V Relay Module [package="Breakout board"]
  VCC2 = Battery block 9V [internal_resistance=0.1Ω]
  M1 = DC Motor [voltage_(max)=6V voltage_(min)=3V]
  VCC1 = Battery block 9V [internal_resistance=0.1Ω]
  Photo_diode = TCRT5000 sensor module [part_number=151608]

nets:
  GND: BME280.GND, LED1.common_cathode, Part3.GND, Display.GND, soil_moisture_sensor.GND, servo.gnd, relai.-, VCC1.-, Photo_diode.T+
  3.3V: BME280.3.3V, Part3.3V3
  N1: BME280.SDI/SDA, Part3.A4, Display.SDA
  N2: BME280.SCK/SCL, Part3.A5, Display.SCL
  N3: LED1.red_anode, R1.Pin_0
  N4: LED1.blue_anode, R2.Pin_0
  N5: LED1.green_anode, R3.Pin_0
  N6: Part3.D2, Photo_diode.D-
  N7: Part3.D3, servo.pulse
  N8: Part3.D4, R1.Pin_1
  N9: Part3.D5, R2.Pin_1
  N10: Part3.D6, R3.Pin_1
  N11: Part3.D7, relai.S
  N12: Part3.VIN, VCC1.+
  VCC: Part3.5V, Display.VCC, soil_moisture_sensor.VCC, servo.vcc, relai.+, Photo_diode.T-
  N13: Part3.A6, soil_moisture_sensor.SIG
  N14: relai.Common, VCC2.+
  N15: relai.NO, M1.pin_1
  N16: VCC2.-, M1.pin_2

notes:
  VCC
  GND
  Do
  Ao

custom parts:
  KY-019 5V Relay Module: KY-019 5V Relay module, used to control AC circuits. (Special thanks to vanepp for fixing the PCB holes and other errors)
  TCRT5000 sensor module: breakout board with TCRT5000
